# Fritzing sketch hardware (saved by Fritzing 1.0.0rc)

parts:
  Mod1 = seeeduino-xiao
  Part2 = Lithium Ion Polymer Battery 3.7v 350mAh [part_number=2750]  # not connected
  Part3 = Adafruit I2C QT Rotary Encoder [part_number="Adafruit #4991"]
  Part6 = OLED Monochrome 128x32 SPI [part_number=661]
  S1 = Pushbutton [package="[THT]"]

nets:
  N1: Mod1.D3, S1.Pin_3, S1.Pin_4
  N2: Mod1.D4, Part3.SDA
  N3: Mod1.D5, Part3.SCL
  N4: Mod1.D7, Part6.CS
  N5: Mod1.D8, Part6.SCLK
  N6: Mod1.D10, Part6.MOSI
  3V3: Mod1.3V3, Part3.VCC

custom parts:
  seeeduino-xiao: Seeeduino XIAO processor board.
  Lithium Ion Polymer Battery 3.7v 350mAh: Lithium ion polymer (also known as 'lipo' or 'lipoly') batteries are thin, light and powerful. The output ranges from 4.2V when completely charged to 3.7V. This battery has a capacity of 350mAh for a total of about 1.3 Wh. The batteries come pre-attached with a genuine 2-pin JST-PH connector as shown and include the necessary protection circuitry.
  Adafruit I2C QT Rotary Encoder: Rotary encoders are soooo much fun! Twist em this way, then twist them that way. Unlike potentiometers, they go all the way around, and often have little detents for tactile feedback. But, if you've ever tried to add encoders to your project you know that they're a real challenge to use: timers, interrupts, debouncing... This Stemma QT breakout makes all that frustration go away - solder in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
  OLED Monochrome 128x32 SPI: These displays are small, only about 1" diagonal, but very readable due to the high contrast of an OLED display. This display is made of 128x32 individual white OLED pixels, each one is turned on or off by the controller chip. Because the display makes its own light, no backlight is required. This reduces the power required to run the OLED and is why the display has such high contrast; we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
